// Logisim project Minimalizacja-Krawczyk-Bartłomiej.circ as structural Verilog: 4 circuits, main circuit main
module main (
  output out_1,
  output out_2,
  output out_3
);

  wire button_1_out;
  wire [4:0] counter_1_q;

  Button button_1 (.out(button_1_out));
  Counter #(.width(5), .max('h1f)) counter_1 (.Q(counter_1_q), .clk(button_1_out));  // open: load, D, count, carry, clr
  APN apn_1 (
    .x4(counter_1_q[4]), .x3(counter_1_q[3]), .x2(counter_1_q[2]), .x1(counter_1_q[1]), .x0(counter_1_q[0]),
    .out_6(out_1));
  KPN kpn_1 (
    .out_6(out_2), .x4(counter_1_q[4]), .x3(counter_1_q[3]), .x2(counter_1_q[2]), .x1(counter_1_q[1]),
    .x0(counter_1_q[0]));
  QMC qmc_1 (.out_5(out_3), .x3(counter_1_q[3]), .x2(counter_1_q[2]), .x1(counter_1_q[1]), .x0(counter_1_q[0]));

  // Notes on the sheet:
  //   Krawczyk Bartłomiej
endmodule

module APN (
  input  x4,
  input  x3,
  input  x2,
  input  x1,
  input  x0,
  output out_6
);

  wire nand_1_out, nand_2_out, nand_3_out, nand_4_out, nand_5_out, not_1_out, not_2_out, not_3_out,
       not_4_out, not_5_out;

  not not_1 (not_1_out, x3);
  not not_2 (not_2_out, x4);
  not not_3 (not_3_out, x2);
  not not_4 (not_4_out, x1);
  not not_5 (not_5_out, x0);
  nand nand_1 (nand_1_out, not_1_out, not_4_out);
  nand nand_2 (nand_2_out, not_1_out, x2);
  nand nand_3 (nand_3_out, x2, x1, x0);
  nand nand_4 (nand_4_out, x4, x2, not_4_out, not_5_out);
  nand nand_5 (nand_5_out, x4, x3, not_3_out, x1, not_5_out);
  nand nand_6 (out_6, nand_1_out, nand_2_out, nand_3_out, nand_4_out, nand_5_out);

  // Notes on the sheet:
  //   Krawczyk Bartłomiej
endmodule

module KPN (
  input  x4,
  input  x3,
  input  x2,
  input  x1,
  input  x0,
  output out_6
);

  wire nor_1_out, nor_2_out, nor_3_out, nor_4_out, nor_5_out, nor_6_out, not_1_out, not_2_out, not_3_out,
       not_4_out;

  not not_1 (not_1_out, x3);
  not not_2 (not_2_out, x2);
  not not_3 (not_3_out, x1);
  not not_4 (not_4_out, x0);
  nor nor_1 (nor_1_out, x3, x2, not_3_out);
  nor nor_2 (nor_2_out, not_1_out, x2, x1);
  nor nor_3 (nor_3_out, not_1_out, x1, not_4_out);
  nor nor_4 (nor_4_out, x4, not_1_out, x0);
  nor nor_5 (nor_5_out, x2, not_3_out, not_4_out);
  nor nor_6 (nor_6_out, not_1_out, not_2_out, not_3_out, x0);
  nor nor_7 (out_6, nor_1_out, nor_2_out, nor_3_out, nor_4_out, nor_5_out, nor_6_out);

  // Notes on the sheet:
  //   Krawczyk Bartłomiej
endmodule

module QMC (
  input  x3,
  input  x2,
  input  x1,
  input  x0,
  output out_5
);

  wire and_1_out, and_2_out, and_3_out, not_1_out, not_2_out, not_3_out, not_4_out;

  not not_1 (not_1_out, x3);
  not not_2 (not_2_out, x1);
  not not_3 (not_3_out, x2);
  not not_4 (not_4_out, x0);
  and and_1 (and_1_out, not_1_out, not_2_out);
  and and_2 (and_2_out, not_1_out, x2);
  and and_3 (and_3_out, x2, x1, x0);
  or or_1 (out_5, and_1_out, and_2_out, and_3_out);

  // Notes on the sheet:
  //   TEST funkcji zminimalizowanej metodą Quine'a-McCluskeya
  //   Krawczyk Bartłomiej
endmodule
