// Logisim project A14.circ as structural Verilog: 2 circuits, main circuit main
module main (
  input  in_1,
  input  in_2,
  input  in_3,
  input  in_4,
  input  in_5,
  input  in_6,
  input  in_7,
  input  in_8,
  input  in_9,
  input  in_10,
  input  in_11,
  input  in_12,
  input  in_13,
  input  in_14,
  input  in_15,
  output out_16
);

  wire a14_1_q0_2, a14_1_q1_2, a14_1_q2_2, a14_2_out_9, a14_2_q0_2, a14_2_q1_2, a14_2_q2_2, a14_3_out_9,
       a14_3_q0_2, a14_3_q1_2, a14_3_q2_2, a14_4_out_9, a14_4_q0_2, a14_4_q1_2, a14_4_q2_2, a14_5_out_9,
       a14_5_q0_2, a14_5_q1_2, a14_5_q2_2, a14_6_out_9, a14_6_q0_2, a14_6_q1_2, a14_6_q2_2, a14_7_out_9,
       a14_7_q0_2, a14_7_q1_2, a14_7_q2_2, a14_8_out_9, a14_8_q0_2, a14_8_q1_2, a14_8_q2_2, a14_9_out_9,
       a14_9_q0_2, a14_9_q1_2, a14_9_q2_2, a14_10_out_9, a14_10_q0_2, a14_10_q1_2, a14_10_q2_2, a14_11_out_9,
       a14_11_q0_2, a14_11_q1_2, a14_11_q2_2;

  A14 a14_1 (
    .q0(in_12), .q1(in_13), .q2(in_15), .out_9(out_16), .a(in_1), .q0_2(a14_1_q0_2), .q1_2(a14_1_q1_2),
    .q2_2(a14_1_q2_2), .p(a14_2_out_9));
  A14 a14_2 (
    .q0(a14_1_q0_2), .q1(a14_1_q1_2), .q2(a14_1_q2_2), .out_9(a14_2_out_9), .a(in_2), .q0_2(a14_2_q0_2),
    .q1_2(a14_2_q1_2), .q2_2(a14_2_q2_2), .p(a14_3_out_9));
  A14 a14_3 (
    .q0(a14_2_q0_2), .q1(a14_2_q1_2), .q2(a14_2_q2_2), .out_9(a14_3_out_9), .a(in_3), .q0_2(a14_3_q0_2),
    .q1_2(a14_3_q1_2), .q2_2(a14_3_q2_2), .p(a14_4_out_9));
  A14 a14_4 (
    .q0(a14_3_q0_2), .q1(a14_3_q1_2), .q2(a14_3_q2_2), .out_9(a14_4_out_9), .a(in_4), .q0_2(a14_4_q0_2),
    .q1_2(a14_4_q1_2), .q2_2(a14_4_q2_2), .p(a14_5_out_9));
  A14 a14_5 (
    .q0(a14_4_q0_2), .q1(a14_4_q1_2), .q2(a14_4_q2_2), .out_9(a14_5_out_9), .a(in_5), .q0_2(a14_5_q0_2),
    .q1_2(a14_5_q1_2), .q2_2(a14_5_q2_2), .p(a14_6_out_9));
  A14 a14_6 (
    .q0(a14_5_q0_2), .q1(a14_5_q1_2), .q2(a14_5_q2_2), .out_9(a14_6_out_9), .a(in_6), .q0_2(a14_6_q0_2),
    .q1_2(a14_6_q1_2), .q2_2(a14_6_q2_2), .p(a14_7_out_9));
  A14 a14_7 (
    .q0(a14_6_q0_2), .q1(a14_6_q1_2), .q2(a14_6_q2_2), .out_9(a14_7_out_9), .a(in_7), .q0_2(a14_7_q0_2),
    .q1_2(a14_7_q1_2), .q2_2(a14_7_q2_2), .p(a14_8_out_9));
  A14 a14_8 (
    .q0(a14_7_q0_2), .q1(a14_7_q1_2), .q2(a14_7_q2_2), .out_9(a14_8_out_9), .a(in_8), .q0_2(a14_8_q0_2),
    .q1_2(a14_8_q1_2), .q2_2(a14_8_q2_2), .p(a14_9_out_9));
  A14 a14_9 (
    .q0(a14_8_q0_2), .q1(a14_8_q1_2), .q2(a14_8_q2_2), .out_9(a14_9_out_9), .a(in_9), .q0_2(a14_9_q0_2),
    .q1_2(a14_9_q1_2), .q2_2(a14_9_q2_2), .p(a14_10_out_9));
  A14 a14_10 (
    .q0(a14_9_q0_2), .q1(a14_9_q1_2), .q2(a14_9_q2_2), .out_9(a14_10_out_9), .a(in_10), .q0_2(a14_10_q0_2),
    .q1_2(a14_10_q1_2), .q2_2(a14_10_q2_2), .p(a14_11_out_9));
  A14 a14_11 (
    .q0(a14_10_q0_2), .q1(a14_10_q1_2), .q2(a14_10_q2_2), .out_9(a14_11_out_9), .a(in_11),
    .q0_2(a14_11_q0_2), .q1_2(a14_11_q1_2), .q2_2(a14_11_q2_2), .p(in_14));
endmodule

module A14 (
  input  a,
  input  q0,
  input  q1,
  input  q2,
  input  p,
  output q0_2,
  output q1_2,
  output q2_2,
  output out_9
);

  wire and_1_out, not_1_out;

  and and_1 (and_1_out, q2, a);
  or or_1 (out_9, and_1_out, p);
  not not_1 (not_1_out, a);
  and and_2 (q1_2, q0, not_1_out);
  and and_3 (q2_2, q1, a);

  assign q0_2 = a;
endmodule
