// Logisim project ITER.circ as structural Verilog: 7 circuits, main circuit main
module main (
  input  in_1,
  input  in_2,
  input  in_3,
  input  in_4,
  input  in_5,
  input  in_6,
  input  in_7,
  input  in_8,
  input  in_9,
  input  in_10,
  input  in_11,
  input  in_12,
  input  in_13,
  input  in_14,
  input  in_15,
  input  in_16,
  input  in_17,
  input  in_18,
  input  in_19,
  input  in_20,
  input  in_21,
  input  in_22,
  input  in_23,
  input  in_24,
  input  in_25,
  input  in_26,
  input  in_27,
  input  in_28,
  input  in_29,
  input  in_30,
  input  in_31,
  input  in_32,
  input  in_33,
  input  in_34,
  input  in_35,
  input  in_36,
  input  in_37,
  input  in_38,
  input  in_39,
  input  in_40,
  input  in_41,
  input  in_42,
  input  in_43,
  input  in_44,
  output out_45,
  output out_46,
  output out_47,
  output out_48,
  output out_49,
  output out_50,
  output out_51,
  output out_52,
  output out_53,
  output out_54,
  output out_55,
  output out_56,
  output out_57,
  output out_58,
  output out_59,
  output out_60,
  output out_61,
  output out_62,
  output out_63,
  output out_64,
  output out_65,
  output out_66,
  output out_67,
  output out_68,
  output out_69,
  output out_70,
  output out_71,
  output out_72,
  output out_73,
  output out_74,
  output out_75,
  output out_76,
  output out_77,
  output out_78
);

  wire iter5_1_q, iter5_2_p_1, iter5_2_q, iter5_3_p_1, iter5_3_q, iter5_4_p_1, iter5_4_q, iter5_5_p_1,
       iter5_5_q, iter5_6_p_1, iter5_6_q, iter5_7_p_1, iter12_1_q0_1, iter12_1_q1_1, iter12_2_q0_1,
       iter12_2_q1_1, iter12_3_q0_1, iter12_3_q1_1, iter12_4_q0_1, iter12_4_q1_1, iter12_5_q0_1,
       iter12_5_q1_1, iter12_6_q0_1, iter12_6_q1_1, iter_1_q0_1, iter_1_q1_1, iter_2_q0_1, iter_2_q1_1,
       iter_3_q0_1, iter_3_q1_1, iterv2_1_q0_1, iterv2_1_q1_1, iterv2_2_p_2, iterv2_2_q0_1, iterv2_2_q1_1,
       iterv2_3_p_2, iterv2_3_q0_1, iterv2_3_q1_1, iterv2_4_p_2, iterv2_4_q0_1, iterv2_4_q1_1, iterv2_5_p_2,
       iterv2_5_q0_1, iterv2_5_q1_1, iterv2_6_p_2;

  MULTI3 multi3_1 (.out_5(out_45), .x2(in_16), .x0(in_19), .x3(in_15), .x1(in_18));
  ITER5 iter5_1 (.p_1(out_61), .q_1(in_35), .p(iter5_2_p_1), .q(iter5_1_q), .a(in_27), .y(out_63));
  ITERv2 iterv2_1 (
    .p_2(out_70), .q1(in_43), .q0(in_44), .p(iterv2_2_p_2), .q1_1(iterv2_1_q1_1), .q0_1(iterv2_1_q0_1),
    .a(in_36), .y(out_73));
  ITER12 iter12_1 (.q1(in_17), .q0(in_20), .q1_1(iter12_1_q1_1), .a(in_1), .b(in_2), .y(out_48), .q0_1(iter12_1_q0_1));
  ITER iter_1 (.q1(in_25), .q0(in_26), .q1_1(iter_1_q1_1), .q0_1(iter_1_q0_1), .a(in_21), .y(out_57));
  ITER5 iter5_2 (.p_1(iter5_2_p_1), .q_1(iter5_1_q), .p(iter5_3_p_1), .q(iter5_2_q), .a(in_28), .y(out_64));
  ITERv2 iterv2_2 (
    .p_2(iterv2_2_p_2), .q1(iterv2_1_q1_1), .q0(iterv2_1_q0_1), .p(iterv2_3_p_2), .q1_1(iterv2_2_q1_1),
    .q0_1(iterv2_2_q0_1), .a(in_37), .y(out_74));
  ITER12 iter12_2 (
    .q1(iter12_1_q1_1), .q0(iter12_1_q0_1), .q1_1(iter12_2_q1_1), .a(in_3), .b(in_4), .y(out_49),
    .q0_1(iter12_2_q0_1));
  ITERv2 iterv2_3 (
    .p_2(iterv2_3_p_2), .q1(iterv2_2_q1_1), .q0(iterv2_2_q0_1), .p(iterv2_4_p_2), .q1_1(iterv2_3_q1_1),
    .q0_1(iterv2_3_q0_1), .a(in_38), .y(out_75));
  ITER12 iter12_3 (
    .q1(iter12_2_q1_1), .q0(iter12_2_q0_1), .q1_1(iter12_3_q1_1), .a(in_5), .b(in_6), .y(out_50),
    .q0_1(iter12_3_q0_1));
  ITER iter_2 (.q1(iter_1_q1_1), .q0(iter_1_q0_1), .q1_1(iter_2_q1_1), .q0_1(iter_2_q0_1), .a(in_22), .y(out_58));
  ITER5 iter5_3 (.p_1(iter5_3_p_1), .q_1(iter5_2_q), .p(iter5_4_p_1), .q(iter5_3_q), .a(in_29), .y(out_65));
  ITER12 iter12_4 (
    .q1(iter12_3_q1_1), .q0(iter12_3_q0_1), .q1_1(iter12_4_q1_1), .a(in_7), .b(in_8), .y(out_51),
    .q0_1(iter12_4_q0_1));
  ITER5 iter5_4 (.p_1(iter5_4_p_1), .q_1(iter5_3_q), .p(iter5_5_p_1), .q(iter5_4_q), .a(in_30), .y(out_66));
  ITERv2 iterv2_4 (
    .p_2(iterv2_4_p_2), .q1(iterv2_3_q1_1), .q0(iterv2_3_q0_1), .p(iterv2_5_p_2), .q1_1(iterv2_4_q1_1),
    .q0_1(iterv2_4_q0_1), .a(in_39), .y(out_76));
  ITER12 iter12_5 (
    .q1(iter12_4_q1_1), .q0(iter12_4_q0_1), .q1_1(iter12_5_q1_1), .a(in_9), .b(in_10), .y(out_52),
    .q0_1(iter12_5_q0_1));
  ITER iter_3 (.q1(iter_2_q1_1), .q0(iter_2_q0_1), .q1_1(iter_3_q1_1), .q0_1(iter_3_q0_1), .a(in_23), .y(out_59));
  ITER5 iter5_5 (.p_1(iter5_5_p_1), .q_1(iter5_4_q), .p(iter5_6_p_1), .q(iter5_5_q), .a(in_31), .y(out_67));
  ITERv2 iterv2_5 (
    .p_2(iterv2_5_p_2), .q1(iterv2_4_q1_1), .q0(iterv2_4_q0_1), .p(iterv2_6_p_2), .q1_1(iterv2_5_q1_1),
    .q0_1(iterv2_5_q0_1), .a(in_40), .y(out_77));
  ITER12 iter12_6 (
    .q1(iter12_5_q1_1), .q0(iter12_5_q0_1), .q1_1(iter12_6_q1_1), .a(in_11), .b(in_12), .y(out_53),
    .q0_1(iter12_6_q0_1));
  ITER iter_4 (.q1(iter_3_q1_1), .q0(iter_3_q0_1), .q1_1(out_55), .q0_1(out_56), .a(in_24), .y(out_60));
  ITERv2 iterv2_6 (
    .p_2(iterv2_6_p_2), .q1(iterv2_5_q1_1), .q0(iterv2_5_q0_1), .p(in_42), .q1_1(out_71), .q0_1(out_72),
    .a(in_41), .y(out_78));
  ITER12 iter12_7 (
    .q1(iter12_6_q1_1), .q0(iter12_6_q0_1), .q1_1(out_46), .a(in_13), .b(in_14), .y(out_54), .q0_1(out_47));
  ITER5 iter5_6 (.p_1(iter5_6_p_1), .q_1(iter5_5_q), .p(iter5_7_p_1), .q(iter5_6_q), .a(in_32), .y(out_68));
  ITER5 iter5_7 (.p_1(iter5_7_p_1), .q_1(iter5_6_q), .p(in_34), .q(out_62), .a(in_33), .y(out_69));
endmodule

module ITER (
  input  a,
  input  q1,
  input  q0,
  output q1_1,
  output q0_1,
  output y
);

  wire and_2_out, not_1_out, not_2_out;

  not not_1 (not_1_out, q1);
  and and_1 (y, not_1_out, a);
  not not_2 (not_2_out, a);
  and and_2 (and_2_out, q0, not_2_out);
  or or_1 (q1_1, and_2_out, q1);
  or or_2 (q0_1, a, q0);
endmodule

module ITER5 (
  input  a,
  input  p,
  input  q_1,
  output p_1,
  output q,
  output y
);

  wire not_1_out, not_2_out;

  or or_1 (p_1, a, p);
  not not_1 (not_1_out, q_1);
  or or_2 (y, not_1_out, a, not_2_out);
  not not_2 (not_2_out, p);
  or or_3 (q, a, q_1);
endmodule

module ITER12 (
  input  a,
  input  b,
  input  q1,
  input  q0,
  output q1_1,
  output q0_1,
  output y
);

  wire and_1_out, and_2_out, and_3_out, and_4_out, not_1_out, not_2_out, not_3_out, not_4_out, not_5_out,
       not_6_out;

  not not_1 (not_1_out, q1);
  and and_1 (and_1_out, a, not_1_out);
  or or_1 (y, and_1_out, and_2_out);
  not not_2 (not_2_out, q0);
  not not_3 (not_3_out, b);
  not not_4 (not_4_out, q0);
  and and_2 (and_2_out, not_4_out, b);
  and and_3 (and_3_out, not_2_out, b, not_5_out);
  not not_5 (not_5_out, a);
  not not_6 (not_6_out, q1);
  or or_2 (q1_1, and_3_out, q1);
  and and_4 (and_4_out, not_3_out, a, not_6_out);
  or or_3 (q0_1, and_4_out, q0);
endmodule

module MULTI3 (
  input  x3,
  input  x2,
  input  x0,
  input  x1,
  output out_5
);

  wire multiplexer_1_out, not_1_out;

  Multiplexer #(.select(2), .enable("false")) multiplexer_1 (
    .in0(1'b1), .in1(1'b1), .in2(1'b0), .in3(1'b1), .out(multiplexer_1_out), .sel({x3, x1}));
  not not_1 (not_1_out, x3);
  Multiplexer #(.select(2), .enable("false")) multiplexer_2 (
    .in0(1'b1), .in1(not_1_out), .in2(1'b0), .in3(multiplexer_1_out), .out(out_5), .sel({x2, x0}));
endmodule

module MULTI4 (
  input  x2,
  input  x0,
  input  x3,
  input  x1,
  output out_5
);

  wire multiplexer_1_out, not_1_out;

  not not_1 (not_1_out, x2);
  Multiplexer #(.enable("false")) multiplexer_1 (.in0(not_1_out), .in1(1'b1), .out(multiplexer_1_out), .sel(x0));
  Multiplexer #(.select(2), .enable("false")) multiplexer_2 (
    .in0(1'b0), .in1(1'b1), .in2(multiplexer_1_out), .in3(x0), .out(out_5), .sel({x3, x1}));
endmodule

module ITERv2 (
  input  a,
  input  p,
  input  q1,
  input  q0,
  output p_2,
  output q1_1,
  output q0_1,
  output y
);

  wire and_1_out, and_2_out, and_3_out, and_4_out, not_1_out, not_2_out, not_3_out;

  not not_1 (not_1_out, q1);
  and and_1 (and_1_out, a, not_1_out, q0);
  not not_2 (not_2_out, q0);
  and and_2 (and_2_out, a, not_2_out, p);
  or or_1 (y, and_1_out, and_2_out);
  not not_3 (not_3_out, a);
  and and_3 (and_3_out, p, a);
  and and_4 (and_4_out, not_3_out, q0);
  or or_2 (q0_1, q0, and_3_out);
  or or_3 (q1_1, q1, and_4_out);

  assign p_2 = a;
endmodule
