// Logisim project Krawczyk Bartłomiej - Lab 2.circ as structural Verilog: 6 circuits, main circuit main
module main (
  input  x7_2,
  input  x6_2,
  input  x5_2,
  input  x4_2,
  input  x3_2,
  input  x2_2,
  input  x1_2,
  input  x0_2,
  input  x7,
  input  x6,
  input  x5,
  input  x4,
  input  x3,
  input  x2,
  input  x1,
  input  x0,
  output y7_2,
  output y6_2,
  output y5_2,
  output y4_2,
  output y3_2,
  output y2_2,
  output y1_2,
  output y0_2,
  output y7,
  output y6,
  output y5,
  output y4,
  output y3,
  output y2,
  output y1,
  output y0
);

  wire a2_1_qi_1, a2_2_p0i_1, a2_2_p1i_1, a2_2_qi_1, a2_3_p0i_1, a2_3_p1i_1, a2_3_qi_1, a2_4_p0i_1,
       a2_4_p1i_1, a2_4_qi_1, a2_5_p0i_1, a2_5_p1i_1, a2_5_qi_1, a2_6_p0i_1, a2_6_p1i_1, a2_6_qi_1,
       a2_7_p0i_1, a2_7_p1i_1, a2_7_qi_1, a2_8_p0i_1, a2_8_p1i_1, a_2_p0i_1, a_2_p1i_1, a_3_p0i_1, a_3_p1i_1,
       a_4_p0i_1, a_4_p1i_1, a_5_p0i_1, a_5_p1i_1, a_6_p0i_1, a_6_p1i_1, a_7_p0i_1, a_7_p1i_1, a_8_p0i_1,
       a_8_p1i_1;

  A a_1 (.p0i(a_2_p0i_1), .p1i(a_2_p1i_1), .xi(x7), .out_6(y7));  // open: p0i_1, p1i_1
  A2 a2_1 (
    .qi(1'b0), .qi_1(a2_1_qi_1), .p0i(a2_2_p0i_1), .p1i(a2_2_p1i_1), .xi(x7_2), .yi(y7_2));  // open: p0i_1, p1i_1
  A a_2 (.p0i_1(a_2_p0i_1), .p1i_1(a_2_p1i_1), .p0i(a_3_p0i_1), .p1i(a_3_p1i_1), .xi(x6), .out_6(y6));
  A2 a2_2 (
    .qi(a2_1_qi_1), .p0i_1(a2_2_p0i_1), .p1i_1(a2_2_p1i_1), .qi_1(a2_2_qi_1), .p0i(a2_3_p0i_1),
    .p1i(a2_3_p1i_1), .xi(x6_2), .yi(y6_2));
  A2 a2_3 (
    .qi(a2_2_qi_1), .p0i_1(a2_3_p0i_1), .p1i_1(a2_3_p1i_1), .qi_1(a2_3_qi_1), .p0i(a2_4_p0i_1),
    .p1i(a2_4_p1i_1), .xi(x5_2), .yi(y5_2));
  A a_3 (.p0i_1(a_3_p0i_1), .p1i_1(a_3_p1i_1), .p0i(a_4_p0i_1), .p1i(a_4_p1i_1), .xi(x5), .out_6(y5));
  A a_4 (.p0i_1(a_4_p0i_1), .p1i_1(a_4_p1i_1), .p0i(a_5_p0i_1), .p1i(a_5_p1i_1), .xi(x4), .out_6(y4));
  A2 a2_4 (
    .qi(a2_3_qi_1), .p0i_1(a2_4_p0i_1), .p1i_1(a2_4_p1i_1), .qi_1(a2_4_qi_1), .p0i(a2_5_p0i_1),
    .p1i(a2_5_p1i_1), .xi(x4_2), .yi(y4_2));
  A2 a2_5 (
    .qi(a2_4_qi_1), .p0i_1(a2_5_p0i_1), .p1i_1(a2_5_p1i_1), .qi_1(a2_5_qi_1), .p0i(a2_6_p0i_1),
    .p1i(a2_6_p1i_1), .xi(x3_2), .yi(y3_2));
  A a_5 (.p0i_1(a_5_p0i_1), .p1i_1(a_5_p1i_1), .p0i(a_6_p0i_1), .p1i(a_6_p1i_1), .xi(x3), .out_6(y3));
  A2 a2_6 (
    .qi(a2_5_qi_1), .p0i_1(a2_6_p0i_1), .p1i_1(a2_6_p1i_1), .qi_1(a2_6_qi_1), .p0i(a2_7_p0i_1),
    .p1i(a2_7_p1i_1), .xi(x2_2), .yi(y2_2));
  A a_6 (.p0i_1(a_6_p0i_1), .p1i_1(a_6_p1i_1), .p0i(a_7_p0i_1), .p1i(a_7_p1i_1), .xi(x2), .out_6(y2));
  A2 a2_7 (
    .qi(a2_6_qi_1), .p0i_1(a2_7_p0i_1), .p1i_1(a2_7_p1i_1), .qi_1(a2_7_qi_1), .p0i(a2_8_p0i_1),
    .p1i(a2_8_p1i_1), .xi(x1_2), .yi(y1_2));
  A a_7 (.p0i_1(a_7_p0i_1), .p1i_1(a_7_p1i_1), .p0i(a_8_p0i_1), .p1i(a_8_p1i_1), .xi(x1), .out_6(y1));
  A2 a2_8 (
    .qi(a2_7_qi_1), .p0i_1(a2_8_p0i_1), .p1i_1(a2_8_p1i_1), .p0i(1'b0), .p1i(1'b0), .xi(x0_2), .yi(y0_2));  // open: qi_1
  A a_8 (.p0i_1(a_8_p0i_1), .p1i_1(a_8_p1i_1), .p0i(1'b0), .p1i(1'b0), .xi(x0), .out_6(y0));

  // Notes on the sheet:
  //   Krawczyk Bartłomiej
  //   Układ szukający grupy co najmniej 2 jedynek
  //   Układ szukający co najmniej 1 jedynki
endmodule

module B (
  input  x3,
  input  x2,
  input  x1,
  input  x0,
  output y1,
  output y2,
  output y3
);

  wire nand_1_out, nand_2_out, nand_3_out, nand_4_out, nand_5_out, nand_6_out, not_1_out, not_2_out,
       not_3_out;

  not not_1 (not_1_out, x3);
  not not_2 (not_2_out, x1);
  not not_3 (not_3_out, x0);
  nand nand_1 (nand_1_out, x3, x0);
  nand nand_2 (nand_2_out, x1, x0);
  nand nand_3 (nand_3_out, x3, not_2_out, not_3_out);
  nand nand_4 (nand_4_out, not_1_out, not_2_out, x0);
  nand nand_5 (nand_5_out, x2, x1, not_3_out);
  nand nand_6 (nand_6_out, x3, x1, x0);
  nand nand_7 (y1, nand_1_out, nand_3_out);
  nand nand_8 (y2, nand_2_out, nand_4_out, nand_3_out);
  nand nand_9 (y3, nand_3_out, nand_4_out, nand_5_out, nand_6_out);
endmodule

module MUX (
  input  x3,
  input  x2,
  input  x1,
  input  x0,
  input  s1,
  input  s0,
  output out_7
);

  wire and_1_out, and_2_out, and_3_out, and_4_out, not_1_out, not_2_out;

  not not_1 (not_1_out, s1);
  not not_2 (not_2_out, s0);
  and and_1 (and_1_out, x3, s0, s1);
  and and_2 (and_2_out, x2, not_2_out, s1);
  and and_3 (and_3_out, x1, s0, not_1_out);
  and and_4 (and_4_out, x0, not_2_out, not_1_out);
  or or_1 (out_7, and_1_out, and_2_out, and_3_out, and_4_out);
endmodule

module C (
  input  x2,
  input  x0,
  input  x1,
  input  x3,
  output y
);

  wire mux_1_out_7;

  MUX mux_1 (.x3(1'b1), .x2(1'b1), .x1(1'b1), .x0(1'b0), .out_7(mux_1_out_7), .s1(x2), .s0(x1));
  MUX mux_2 (.x3(mux_1_out_7), .x2(1'b0), .x1(x2), .x0(1'b1), .out_7(y), .s1(x3), .s0(x0));
endmodule

module A (
  input  xi,
  input  p0i,
  input  p1i,
  output p0i_1,
  output p1i_1,
  output out_6
);

  wire and_1_out, not_1_out, not_2_out;

  or or_1 (p0i_1, p0i, xi);
  or or_2 (p1i_1, and_1_out, p1i);
  and and_1 (and_1_out, not_1_out, p0i);
  not not_1 (not_1_out, xi);
  and and_2 (out_6, xi, not_2_out);
  not not_2 (not_2_out, p1i);
endmodule

module A2 (
  input  xi,
  input  qi,
  input  p0i,
  input  p1i,
  output qi_1,
  output p0i_1,
  output p1i_1,
  output yi
);

  wire and_1_out, and_2_out, and_3_out, and_4_out, not_1_out, not_2_out;

  or or_1 (p0i_1, p0i, and_1_out);
  or or_2 (p1i_1, p1i, and_2_out);
  and and_1 (and_1_out, xi, qi);
  not not_1 (not_1_out, xi);
  and and_2 (and_2_out, not_1_out, p0i);
  and and_3 (and_3_out, qi, not_2_out, xi);
  and and_4 (and_4_out, xi, not_2_out, p0i);
  or or_3 (yi, and_3_out, and_4_out);
  not not_2 (not_2_out, p1i);

  assign qi_1 = xi;
endmodule
