// Logisim project xD.circ as structural Verilog
module A2 (
  output y2,
  output y1,
  output y0
);

  wire clock_1_out, D2_qn;

  Clock clock_1 (.out(clock_1_out));
  D_Flip_Flop D2 (.clk(clock_1_out), .D(y1), .Q(y2), .Qn(D2_qn));  // open: preset, en, reset
  D_Flip_Flop D1 (.clk(clock_1_out), .D(y0), .Q(y1));  // open: Qn, preset, en, reset
  D_Flip_Flop D0 (.clk(clock_1_out), .D(D2_qn), .Q(y0));  // open: Qn, preset, en, reset
endmodule

module A4 (
  output y2,
  output y1,
  output y0
);

  wire and_1_out, and_2_out, and_3_out, and_4_out, clock_1_out, D0_qn, D1_qn, D2_qn, or_1_out, or_2_out,
       or_3_out;

  and and_1 (and_1_out, y1, D0_qn);
  and and_2 (and_2_out, D1_qn, y0);
  and and_3 (and_3_out, D2_qn, D0_qn);
  or or_1 (or_1_out, and_3_out, and_4_out);
  and and_4 (and_4_out, D1_qn, D0_qn);
  or or_2 (or_2_out, D1_qn, y0);
  or or_3 (or_3_out, and_1_out, and_2_out);
  Clock clock_1 (.out(clock_1_out));
  D_Flip_Flop D2 (.clk(clock_1_out), .D(or_2_out), .Q(y2), .Qn(D2_qn));  // open: preset, en, reset
  D_Flip_Flop D1 (.clk(clock_1_out), .D(or_3_out), .Q(y1), .Qn(D1_qn));  // open: preset, en, reset
  D_Flip_Flop D0 (.clk(clock_1_out), .D(or_1_out), .Q(y0), .Qn(D0_qn));  // open: preset, en, reset
endmodule

module A6 (
  output y2,
  output y1,
  output y,
  output y0
);

  wire and_1_out, and_2_out, and_3_out, and_4_out, and_5_out, and_6_out, and_7_out, button_1_out, D0_qn,
       D1_qn, D2_qn, or_1_out, or_2_out, or_3_out;

  and and_1 (and_1_out, y2, y0);
  and and_2 (and_2_out, y2, y1);
  and and_3 (and_3_out, y1, y0);
  and and_4 (and_4_out, D2_qn, y1);
  and and_5 (and_5_out, y2, D0_qn);
  D_Flip_Flop D2 (.clk(button_1_out), .D(or_1_out), .Q(y2), .Qn(D2_qn));  // open: preset, en, reset
  or or_1 (or_1_out, and_1_out, and_2_out, and_3_out);
  D_Flip_Flop D1 (.clk(button_1_out), .D(or_2_out), .Q(y1), .Qn(D1_qn));  // open: preset, en, reset
  or or_2 (or_2_out, D2_qn, and_3_out);
  D_Flip_Flop D0 (.clk(button_1_out), .D(or_3_out), .Q(y0), .Qn(D0_qn));  // open: preset, en, reset
  or or_3 (or_3_out, and_4_out, and_5_out);
  Button button_1 (.out(button_1_out));
  and and_6 (and_6_out, y2, D1_qn, y0);
  and and_7 (and_7_out, D2_qn, y1, D0_qn);
  or or_4 (y, and_6_out, and_7_out);
endmodule

module B5 (
  input  x,
  input  z,
  output y
);

  wire b2_d0_1_d0, b5_d1_1_d1, b5_d2_1_d2, button_1_out, D0_q, D1_q, D1_qn, D2_q;

  B5_D2 b5_d2_1 (.Q2(D2_q), .Q1(D1_q), .Q0(D0_q), .z(z), .D2(b5_d2_1_d2));
  B5_D1 b5_d1_1 (.Q2(D2_q), .Q1(D1_q), .Q0(D0_q), .x(x), .z(x), .D1(b5_d1_1_d1));
  B2_D0 b2_d0_1 (.Q2(D2_q), .Q1(D1_q), .Q0(D0_q), .x(x), .z(z), .D0(b2_d0_1_d0));
  Button button_1 (.out(button_1_out));
  D_Flip_Flop D2 (.clk(button_1_out), .D(b5_d2_1_d2), .Q(D2_q));  // open: Qn, preset, en, reset
  D_Flip_Flop D1 (.clk(button_1_out), .D(b5_d1_1_d1), .Q(D1_q), .Qn(D1_qn));  // open: preset, en, reset
  D_Flip_Flop D0 (.clk(button_1_out), .D(b2_d0_1_d0), .Q(D0_q));  // open: Qn, preset, en, reset
  and and_1 (y, D2_q, D1_qn);
endmodule

module B5_D2 (
  input  Q2,
  input  Q1,
  input  Q0,
  input  z,
  output D2
);

  wire and_1_out, and_2_out, not_1_out, not_2_out, not_3_out;

  not not_1 (not_1_out, Q2);
  not not_2 (not_2_out, z);
  and and_1 (and_1_out, not_1_out, Q1, Q0, not_2_out);
  and and_2 (and_2_out, Q2, not_3_out, not_2_out);
  not not_3 (not_3_out, Q0);
  or or_1 (D2, and_1_out, and_2_out);
endmodule

module B5_D1 (
  input  Q2,
  input  Q1,
  input  Q0,
  input  x,
  input  z,
  output D1
);

  wire and_1_out, and_2_out, not_1_out, not_2_out, not_3_out;

  not not_1 (not_1_out, Q2);
  not not_2 (not_2_out, Q1);
  not not_3 (not_3_out, z);
  and and_1 (and_1_out, not_2_out, x, not_3_out);
  and and_2 (and_2_out, not_1_out, Q0, not_3_out);
  or or_1 (D1, and_1_out, and_2_out);
endmodule

module B2_D0 (
  input  Q2,
  input  Q1,
  input  Q0,
  input  x,
  input  z,
  output D0
);

  wire not_1_out, not_2_out, not_3_out, not_4_out, not_5_out, or_1_out, or_2_out, or_3_out, or_4_out;

  not not_1 (not_1_out, Q2);
  not not_2 (not_2_out, Q1);
  not not_3 (not_3_out, Q0);
  not not_4 (not_4_out, z);
  not not_5 (not_5_out, x);
  or or_1 (or_1_out, Q2, Q1, not_3_out);
  or or_2 (or_2_out, not_2_out, not_1_out, Q0);
  or or_3 (or_3_out, Q2, not_2_out, not_3_out, x);
  or or_4 (or_4_out, not_2_out, Q2, Q0, not_5_out);
  and and_1 (D0, or_1_out, or_2_out, or_3_out, or_4_out, not_4_out);
endmodule

module A9 (
  input  x,
  output y
);

  wire and_1_out, b9_d0_1_out_5, button_1_out, button_2_out, D0_q, D1_q, D2_q, not_1_out, not_2_out;

  not not_1 (not_1_out, D2_q);
  and and_1 (and_1_out, not_1_out, D1_q);
  not not_2 (not_2_out, D2_q);
  B9_D0 b9_d0_1 (.Q2(D2_q), .Q1(D1_q), .Q0(D0_q), .x(x), .out_5(b9_d0_1_out_5));
  Button button_1 (.out(button_1_out));
  D_Flip_Flop D2 (.clk(button_1_out), .D(and_1_out), .Q(D2_q), .reset(button_2_out));  // open: Qn, preset, en
  D_Flip_Flop D1 (.clk(button_1_out), .D(not_2_out), .Q(D1_q), .reset(button_2_out));  // open: Qn, preset, en
  D_Flip_Flop D0 (.clk(button_1_out), .D(b9_d0_1_out_5), .Q(D0_q), .reset(button_2_out));  // open: Qn, preset, en
  Button button_2 (.out(button_2_out));
  and and_2 (y, D2_q, D0_q);
endmodule

module B9_D0 (
  input  Q2,
  input  Q1,
  input  Q0,
  input  x,
  output out_5
);

  wire and_1_out, and_2_out, and_3_out, and_4_out, not_1_out, not_2_out, not_3_out, not_4_out;

  not not_1 (not_1_out, Q2);
  not not_2 (not_2_out, Q1);
  not not_3 (not_3_out, Q0);
  not not_4 (not_4_out, x);
  and and_1 (and_1_out, not_4_out, not_3_out, not_1_out);
  and and_2 (and_2_out, not_2_out, Q0);
  and and_3 (and_3_out, x, Q2);
  and and_4 (and_4_out, x, Q0);
  or or_1 (out_5, and_1_out, and_2_out, and_3_out, and_4_out);
endmodule

module C1 (
  input  x1,
  input  x0,
  output out_3,
  output out_4
);

  wire button_1_out, multiplexer_1_out, multiplexer_2_out, not_1_out;

  not not_1 (not_1_out, out_3);
  Multiplexer #(.select(3)) multiplexer_1 (
    .in0(1'b0), .in1(1'b1), .in2(1'b1), .in3(1'b1), .in4(1'b0), .in5(1'b0), .in6(1'b0), .in7(1'b1),
    .out(multiplexer_1_out), .sel({out_3, x1, x0}));  // open: en
  Multiplexer #(.select(3)) multiplexer_2 (
    .in0(1'b0), .in1(not_1_out), .in2(out_3), .in3(1'b0), .in4(1'b0), .in5(out_3), .in6(not_1_out),
    .in7(1'b0), .out(multiplexer_2_out), .sel({out_4, x1, x0}));  // open: en
  Button button_1 (.out(button_1_out));
  D_Flip_Flop d_ff_1 (.clk(button_1_out), .D(multiplexer_1_out), .Q(out_3));  // open: Qn, preset, en, reset
  D_Flip_Flop d_ff_2 (.clk(button_1_out), .D(multiplexer_2_out), .Q(out_4));  // open: Qn, preset, en, reset
endmodule
