// Logisim project Krawczyk Bartłomiej - Lab 3.circ as structural Verilog
module _2 (
  input  x1,
  input  x0,
  output y,
  output Q2,
  output Q1,
  output Q0
);

  wire clock_1_out, j_k_ff_1_qn, j_k_ff_2_qn, j_k_ff_3_qn, nand_1_out, nand_2_out, nand_3_out, nand_4_out,
       nand_5_out, nand_6_out, nand_7_out, nand_8_out, nand_9_out, nand_10_out, nand_11_out, nand_12_out,
       nand_13_out, nand_14_out, nand_15_out, not_1_out, not_2_out, not_3_out;

  not not_1 (not_1_out, x1);
  not not_2 (not_2_out, x0);
  nand nand_1 (nand_1_out, x1, not_2_out);
  not not_3 (not_3_out, nand_2_out);
  nand nand_2 (nand_2_out, not_2_out, Q1);
  nand nand_3 (nand_3_out, not_1_out, j_k_ff_3_qn);
  nand nand_4 (nand_4_out, x1, Q0);
  nand nand_5 (nand_5_out, not_2_out, j_k_ff_1_qn, Q0);
  nand nand_6 (nand_6_out, not_2_out, j_k_ff_1_qn);
  nand nand_7 (nand_7_out, j_k_ff_1_qn, j_k_ff_2_qn);
  nand nand_8 (nand_8_out, j_k_ff_1_qn, not_1_out);
  nand nand_9 (nand_9_out, Q2, Q1, x1);
  Clock clock_1 (.out(clock_1_out));
  J_K_Flip_Flop j_k_ff_1 (
    .J(not_3_out), .clk(clock_1_out), .K(nand_10_out), .Q(Q2), .Qn(j_k_ff_1_qn));  // open: preset, en, reset
  nand nand_10 (nand_10_out, not_2_out, Q1, nand_3_out, nand_4_out);
  nand nand_11 (nand_11_out, nand_1_out, nand_5_out);
  J_K_Flip_Flop j_k_ff_2 (
    .J(nand_11_out), .clk(clock_1_out), .K(nand_12_out), .Q(Q1), .Qn(j_k_ff_2_qn));  // open: preset, en, reset
  nand nand_12 (nand_12_out, not_2_out, j_k_ff_1_qn, Q0);
  nand nand_13 (nand_13_out, nand_1_out, nand_6_out);
  J_K_Flip_Flop j_k_ff_3 (
    .J(nand_13_out), .clk(clock_1_out), .K(nand_14_out), .Q(Q0), .Qn(j_k_ff_3_qn));  // open: preset, en, reset
  nand nand_14 (nand_14_out, not_2_out, nand_7_out, nand_8_out, nand_9_out);
  nand nand_15 (nand_15_out, Q2, j_k_ff_2_qn);
  not not_4 (y, nand_15_out);

  // Notes on the sheet:
  //   Bartłomiej Krawczyk
endmodule

module _1 (
  input  x1,
  input  x0,
  output L1,
  output L0
);

  wire clock_1_out, d_ff_1_qn, d_ff_2_qn, multiplexer_1_out, multiplexer_2_out, not_1_out, not_2_out;

  not not_1 (not_1_out, x1);
  not not_2 (not_2_out, x0);
  Clock clock_1 (.out(clock_1_out));
  Multiplexer #(.select(2), .enable("false")) multiplexer_1 (
    .in0(1'b1), .in1(d_ff_1_qn), .in2(d_ff_1_qn), .in3(d_ff_1_qn), .out(multiplexer_1_out), .sel({x1, x0}));
  Multiplexer #(.select(3), .enable("false")) multiplexer_2 (
    .in0(1'b1), .in1(not_2_out), .in2(not_2_out), .in3(1'b1), .in4(x0), .in5(not_2_out), .in6(1'b1),
    .in7(1'b0), .out(multiplexer_2_out), .sel({x1, L1, L0}));
  D_Flip_Flop d_ff_1 (.clk(clock_1_out), .D(multiplexer_1_out), .Q(L1), .Qn(d_ff_1_qn));  // open: preset, en, reset
  D_Flip_Flop d_ff_2 (.clk(clock_1_out), .D(multiplexer_2_out), .Q(L0), .Qn(d_ff_2_qn));  // open: preset, en, reset

  // Notes on the sheet:
  //   Bartłomiej Krawczyk
endmodule
