// Logisim project Sekwencja.circ as structural Verilog: 1 circuit, main circuit main
module main (
  input  x1,
  input  x0,
  output y
);

  wire and_1_out, and_2_out, and_3_out, and_4_out, and_5_out, and_6_out, and_7_out, and_8_out, and_9_out,
       and_10_out, not_1_out, not_2_out, not_3_out, not_4_out, or_1_out, or_2_out;

  not not_1 (not_1_out, x1);
  not not_2 (not_2_out, x0);
  not not_3 (not_3_out, or_2_out);
  not not_4 (not_4_out, y);
  and and_1 (and_1_out, x1, x0, not_3_out);
  and and_2 (and_2_out, not_2_out, or_1_out, not_4_out);
  and and_3 (and_3_out, or_1_out, not_3_out);
  and and_4 (and_4_out, x1, not_2_out);
  and and_5 (and_5_out, not_2_out, y);
  and and_6 (and_6_out, x0, or_2_out, not_4_out);
  and and_7 (and_7_out, not_1_out, or_1_out);
  and and_8 (and_8_out, x1, or_2_out, not_4_out);
  and and_9 (and_9_out, not_1_out, not_2_out, or_1_out);
  and and_10 (and_10_out, not_1_out, or_2_out, y);
  or or_1 (or_1_out, and_1_out, and_2_out, and_3_out);
  or or_2 (or_2_out, and_4_out, and_5_out, and_6_out, and_7_out, and_8_out);
  or or_3 (y, and_9_out, and_10_out);
endmodule
