// Logisim project funkcja.circ as structural Verilog: 1 circuit, main circuit main
module main (
  input  [3:0] ai,
  input  [3:0] bi,
  input  SYNC,
  output ACK,
  output Y
);

  wire clock_1_out, counter_1_carry, counter_2_carry, multiplexer_1_out, nand_1_out, not_1_out, not_2_out,
       not_3_out, not_4_out, not_5_out, or_1_out;
  wire [2:0] rom_1_data_3;
  wire [3:0] counter_3_q, rom_1_data;
  wire [6:0] adder_1_out;
  wire [7:0] adder_3_out, xor_1_out;
  wire [8:0] adder_2_out, register_1_q;
  wire [11:4] rom_1_data_2;

  Adder #(.width(7)) adder_1 (
    .a({{4{bi[3]}}, bi[2:0]}), .b({{2{ai[3]}}, ai[2:0], 2'b00}), .out(adder_1_out), .cin(1'b0));  // open: cout
  Adder #(.width(9)) adder_2 (
    .a({{3{adder_1_out[6]}}, adder_1_out[5:0]}), .b(register_1_q), .out(adder_2_out), .cin(1'b0));  // open: cout
  Register #(.width(9)) register_1 (
    .D(adder_2_out), .en(rom_1_data_2[5]), .Q(register_1_q), .clk(clock_1_out), .clr(rom_1_data_2[4]));
  assign xor_1_out = {8{register_1_q[8]}} ^ register_1_q[7:0];  // XOR_Gate xor_1, 8 bits wide
  Adder adder_3 (.a(xor_1_out), .b({8{1'b0}}), .out(adder_3_out), .cin(register_1_q[8]));  // open: cout
  Clock clock_1 (.out(clock_1_out));
  or or_1 (or_1_out, rom_1_data_2[9], rom_1_data_2[8]);
  Counter counter_1 (
    .load(or_1_out), .D(adder_3_out), .count(rom_1_data_2[8]), .carry(counter_1_carry), .clk(clock_1_out));  // open: Q, clr
  Counter #(.width(3), .max('h4)) counter_2 (
    .count(rom_1_data_2[6]), .carry(counter_2_carry), .clk(clock_1_out), .clr(rom_1_data_2[7]));  // open: load, D, Q
  not not_1 (not_1_out, SYNC);
  not not_2 (not_2_out, counter_2_carry);
  not not_3 (not_3_out, counter_1_carry);
  not not_4 (not_4_out, clock_1_out);
  Multiplexer #(.select(3), .enable("false")) multiplexer_1 (
    .in0(SYNC), .in1(not_1_out), .in2(not_2_out), .in3(counter_1_carry), .in4(not_3_out), .in5(1'b1),
    .in6(1'b0), .in7(1'b0), .out(multiplexer_1_out), .sel(rom_1_data_3));
  not not_5 (not_5_out, multiplexer_1_out);
  Counter #(.width(4), .max('h7)) counter_3 (
    .load(not_5_out), .D(rom_1_data), .count(multiplexer_1_out), .Q(counter_3_q), .clk(not_4_out));  // open: carry, clr
  nand nand_1 (nand_1_out, rom_1_data_2[11], ACK);
  nand nand_2 (ACK, nand_1_out, rom_1_data_2[10]);
  ROM #(.addrWidth(4), .dataWidth(15)) rom_1 (
    .addr(counter_3_q), .data({rom_1_data_3, rom_1_data_2, rom_1_data}));  // open: sel
  and and_1 (Y, clock_1_out, rom_1_data_2[8]);

  // Notes on the sheet:
  //   contents of rom_1 (hex, n*v repeats v):
  //   5c90 401 2c65 1803 6c01 4e07 3d06 1807 6c00
endmodule
