// Logisim project mnożenie.circ as structural Verilog: 3 circuits, main circuit main
module main (
  input  [3:0] in_1,
  input  in_2,
  input  [3:0] in_3,
  input  in_4,
  output out_5,
  output [7:0] out_6
);

  wire \układ_sterujący_1_s0 , \układ_sterujący_1_s1 , \układ_sterujący_1_s2 , \układ_sterujący_1_s3 ,
       \układ_wykonawczy_1_l0 , \układ_wykonawczy_1_mk0_2 ;

  Hex_Digit_Display hex_digit_display_1 (.value(out_6[7:4]));  // open: dp
  Hex_Digit_Display hex_digit_display_2 (.value(out_6[3:0]));  // open: dp
  \Układ_wykonawczy  \układ_wykonawczy_1  (
    .MK0(in_3[0]), .MK1(in_3[1]), .MK2(in_3[2]), .MK3(in_3[3]), .ACK(out_5), .S0(\układ_sterujący_1_s0 ),
    .S1(\układ_sterujący_1_s1 ), .S2(\układ_sterujący_1_s2 ), .S3(\układ_sterujący_1_s3 ), .out_14(out_6),
    .MK0_2(\układ_wykonawczy_1_mk0_2 ), .L0(\układ_wykonawczy_1_l0 ), .MN3(in_1[3]), .MN2(in_1[2]),
    .MN1(in_1[1]), .MN0(in_1[0]));
  \Układ_sterujący  \układ_sterujący_1  (
    .S0(\układ_sterujący_1_s0 ), .S1(\układ_sterujący_1_s1 ), .S2(\układ_sterujący_1_s2 ),
    .S3(\układ_sterujący_1_s3 ), .W0(\układ_wykonawczy_1_mk0_2 ), .W1(\układ_wykonawczy_1_l0 ), .SYNC(in_2),
    .in_4(in_4));
endmodule

module \Układ_wykonawczy  (
  input  MK0,
  input  MK1,
  input  MK2,
  input  MK3,
  input  MN3,
  input  MN2,
  input  MN1,
  input  MN0,
  input  S0,
  input  S1,
  input  S2,
  input  S3,
  output ACK,
  output [7:0] out_14,
  output MK0_2,
  output L0
);

  wire adder_1_cout, clock_1_out, not_1_out, not_2_out, not_3_out, RH_out;
  wire [3:0] adder_1_out, MN_q, multiplexer_1_out;

  Shift_Register #(.length(4)) RH (
    .shift(S2), .in(adder_1_cout), .clk(not_1_out), .out(RH_out), .load(S1), .clr(S0), .d0(adder_1_out[3]),
    .q0(out_14[7]), .d1(adder_1_out[2]), .q1(out_14[6]), .d2(adder_1_out[1]), .q2(out_14[5]),
    .d3(adder_1_out[0]), .q3(out_14[4]));
  Shift_Register #(.length(4)) MK (
    .shift(S2), .in(RH_out), .clk(not_1_out), .load(S0), .d0(MK3), .q0(out_14[3]), .d1(MK2), .q1(out_14[2]),
    .d2(MK1), .q2(out_14[1]), .d3(MK0), .q3(MK0_2));  // open: out, clr
  Adder #(.width(4)) adder_1 (
    .a(multiplexer_1_out), .b(out_14[7:4]), .out(adder_1_out), .cout(adder_1_cout));  // open: cin
  Multiplexer #(.width(4), .enable("false")) multiplexer_1 (
    .in0(4'b0000), .in1(MN_q), .out(multiplexer_1_out), .sel(MK0_2));
  Register #(.width(4)) MN (.D({MN3, MN2, MN1, MN0}), .en(S0), .Q(MN_q), .clk(not_1_out));  // open: clr
  Clock clock_1 (.out(clock_1_out));
  not not_1 (not_1_out, clock_1_out);
  Counter #(.width(3), .max('h4)) counter_1 (.count(S2), .carry(L0), .clk(not_1_out), .clr(S0));  // open: load, D, Q
  not not_2 (not_2_out, S0);
  D_Flip_Flop d_ff_1 (.Q(ACK), .preset(not_2_out), .reset(not_3_out));  // open: clk, D, Qn, en
  not not_3 (not_3_out, S3);

  assign out_14[0] = MK0_2;
endmodule

module \Układ_sterujący  (
  input  SYNC,
  input  W0,
  input  W1,
  input  in_4,
  output S0,
  output S1,
  output S2,
  output S3
);

  wire and_1_out, and_2_out, and_3_out, and_4_out, and_5_out, and_6_out, and_7_out, and_8_out, clock_1_out,
       d_ff_3_q, not_1_out, not_2_out, not_3_out, not_4_out, or_1_out, or_2_out, or_3_out, or_4_out;

  Clock clock_1 (.out(clock_1_out));
  or or_1 (or_1_out, and_7_out, and_2_out);
  D_Flip_Flop d_ff_1 (.clk(clock_1_out), .D(or_1_out), .Q(S0), .preset(in_4));  // open: Qn, en, reset
  not not_1 (not_1_out, SYNC);
  and and_1 (and_1_out, SYNC, S0);
  and and_2 (and_2_out, not_1_out, S0);
  or or_2 (or_2_out, and_1_out, and_6_out);
  and and_3 (and_3_out, W0, or_2_out);
  not not_2 (not_2_out, W0);
  and and_4 (and_4_out, not_2_out, or_2_out);
  D_Flip_Flop d_ff_2 (.clk(clock_1_out), .D(and_3_out), .Q(S1));  // open: Qn, preset, en, reset
  D_Flip_Flop d_ff_3 (.clk(clock_1_out), .D(and_4_out), .Q(d_ff_3_q));  // open: Qn, preset, en, reset
  or or_3 (or_3_out, S1, d_ff_3_q);
  D_Flip_Flop d_ff_4 (.clk(clock_1_out), .D(or_3_out), .Q(S2));  // open: Qn, preset, en, reset
  and and_5 (and_5_out, W1, S2);
  not not_3 (not_3_out, W1);
  and and_6 (and_6_out, not_3_out, S2);
  not not_4 (not_4_out, SYNC);
  and and_7 (and_7_out, not_4_out, S3);
  and and_8 (and_8_out, S3, SYNC);
  or or_4 (or_4_out, and_8_out, and_5_out);
  D_Flip_Flop d_ff_5 (.clk(clock_1_out), .D(or_4_out), .Q(S3));  // open: Qn, preset, en, reset
endmodule
