// Logisim project mnożenie2.circ as structural Verilog: 1 circuit, main circuit main
module main (
  input  [3:0] ARG_1_MK,
  input  [3:0] ARG_1_MK_2,
  input  SYNC,
  output WYN,
  output ACK,
  output [7:0] WYNIK__ILOCZYN
);

  wire adder_1_cout, and_1_out, CK_out, d_ff_1_q, multiplexer_2_out, nand_1_out, not_1_out, not_2_out,
       not_3_out, not_4_out, not_5_out, shift_register_1_out;
  wire [2:0] counter_1_q, counter_2_q, rom_1_data, rom_1_data_3;
  wire [3:0] adder_1_out, multiplexer_1_out, shift_register_3_q3;
  wire [6:3] rom_1_data_2;

  Shift_Register #(.length(4)) shift_register_1 (
    .shift(rom_1_data_2[5]), .in(d_ff_1_q), .clk(CK_out), .out(shift_register_1_out), .load(rom_1_data_2[4]),
    .clr(rom_1_data_2[3]), .d0(adder_1_out[3]), .q0(WYNIK__ILOCZYN[7]), .d1(adder_1_out[2]),
    .q1(WYNIK__ILOCZYN[6]), .d2(adder_1_out[1]), .q2(WYNIK__ILOCZYN[5]), .d3(adder_1_out[0]),
    .q3(WYNIK__ILOCZYN[4]));
  D_Flip_Flop d_ff_1 (.clk(CK_out), .D(adder_1_cout), .Q(d_ff_1_q));  // open: Qn, preset, en, reset
  Shift_Register #(.length(4)) shift_register_2 (
    .shift(rom_1_data_2[5]), .in(shift_register_1_out), .clk(CK_out), .load(rom_1_data_2[3]),
    .d0(ARG_1_MK[3]), .q0(WYNIK__ILOCZYN[3]), .d1(ARG_1_MK[2]), .q1(WYNIK__ILOCZYN[2]), .d2(ARG_1_MK[1]),
    .q2(WYNIK__ILOCZYN[1]), .d3(ARG_1_MK[0]), .q3(WYNIK__ILOCZYN[0]));  // open: out, clr
  Adder #(.width(4)) adder_1 (
    .a(multiplexer_1_out), .b(WYNIK__ILOCZYN[7:4]), .out(adder_1_out), .cin(1'b0), .cout(adder_1_cout));
  Shift_Register #(.length(4)) shift_register_3 (
    .shift(1'b0), .clk(CK_out), .load(rom_1_data_2[3]), .d0(ARG_1_MK_2[3]), .q0(shift_register_3_q3[3]),
    .d1(ARG_1_MK_2[2]), .q1(shift_register_3_q3[2]), .d2(ARG_1_MK_2[1]), .q2(shift_register_3_q3[1]),
    .d3(ARG_1_MK_2[0]), .q3(shift_register_3_q3[0]));  // open: in, out, clr
  Multiplexer #(.width(4), .enable("false")) multiplexer_1 (
    .in0(4'b0000), .in1(shift_register_3_q3), .out(multiplexer_1_out), .sel(WYNIK__ILOCZYN[0]));
  Clock CK (.out(CK_out));
  Counter #(.width(3), .max('h7)) counter_1 (
    .load(1'b0), .count(rom_1_data_2[5]), .Q(counter_1_q), .clk(CK_out), .clr(rom_1_data_2[3]));  // open: D, carry
  not not_1 (not_1_out, CK_out);
  and and_1 (and_1_out, ~counter_1_q[0], ~counter_1_q[1], counter_1_q[2]);  // AND_Gate
  not not_2 (not_2_out, SYNC);
  Multiplexer #(.select(3), .enable("false")) multiplexer_2 (
    .in0(SYNC), .in1(not_2_out), .in2(WYNIK__ILOCZYN[0]), .in3(and_1_out), .in4(1'b1), .in5(1'b0),
    .in6(1'b0), .in7(1'b0), .out(multiplexer_2_out), .sel(rom_1_data_3));
  not not_3 (not_3_out, multiplexer_2_out);
  not not_4 (not_4_out, rom_1_data_2[3]);
  not not_5 (not_5_out, rom_1_data_2[6]);
  Counter #(.width(3), .max('h7)) counter_2 (
    .load(not_3_out), .D(rom_1_data), .count(multiplexer_2_out), .Q(counter_2_q), .clk(not_1_out));  // open: carry, clr
  nand nand_1 (nand_1_out, not_4_out, ACK);
  nand nand_2 (ACK, nand_1_out, not_5_out);
  ROM #(.addrWidth(3), .dataWidth(10)) rom_1 (
    .addr(counter_2_q), .data({rom_1_data_3, rom_1_data_2, rom_1_data}));  // open: sel

  assign WYN = ACK;

  // Notes on the sheet:
  //   S1
  //   S2
  //   S0
  //   contents of rom_1 (hex, n*v repeats v):
  //   8 103 210 1a1 c4 280
endmodule
