// Logisim project suma znak moduł.circ as structural Verilog: 3 circuits, main circuit main
module main (
  input  [3:0] in_1,
  input  [3:0] in_2,
  input  Sync,
  input  Set,
  output [3:0] out_5,
  output ACK
);

  wire \układ_sterujący_1_s0 , \układ_sterujący_1_s1 , \układ_sterujący_1_s2 , \układ_sterujący_1_s3 ,
       \układ_wykonawczy_1_w0 , \układ_wykonawczy_1_w1 ;

  \Układ_wykonawczy  \układ_wykonawczy_1  (
    .A(in_1), .B(in_2), .out_9(out_5), .W0(\układ_wykonawczy_1_w0 ), .W1(\układ_wykonawczy_1_w1 ),
    .S0(\układ_sterujący_1_s0 ), .S1(\układ_sterujący_1_s1 ), .S2(\układ_sterujący_1_s2 ),
    .S3(\układ_sterujący_1_s3 ));
  \Układ_sterujący  \układ_sterujący_1  (
    .W0(\układ_wykonawczy_1_w0 ), .W1(\układ_wykonawczy_1_w1 ), .S0(\układ_sterujący_1_s0 ),
    .S1(\układ_sterujący_1_s1 ), .S2(\układ_sterujący_1_s2 ), .S3(\układ_sterujący_1_s3 ), .SYNC(Sync),
    .Set(Set), .ACK(ACK));
endmodule

module \Układ_wykonawczy  (
  input  [3:0] B,
  input  [3:0] A,
  input  S0,
  input  S1,
  input  S2,
  input  S3,
  output W0,
  output W1,
  output [3:0] out_9
);

  wire clock_1_out, multiplexer_1_out, not_1_out, ZA_q, ZB_q;
  wire [2:0] adder_1_out, MA_q, MB_q, multiplexer_2_out, multiplexer_3_out, multiplexer_4_out,
       subtractor_1_out;

  Clock clock_1 (.out(clock_1_out));
  Register #(.width(1)) ZA (.D(A[3]), .en(S0), .Q(ZA_q), .clk(clock_1_out));  // open: clr
  Multiplexer #(.enable("false")) multiplexer_1 (.in0(ZA_q), .in1(ZB_q), .out(multiplexer_1_out), .sel(not_1_out));
  Register #(.width(3)) MA (.D(A[2:0]), .en(S0), .Q(MA_q), .clk(clock_1_out));  // open: clr
  Register #(.width(1)) ZW (.D(multiplexer_1_out), .en(S3), .Q(out_9[3]), .clk(clock_1_out));  // open: clr
  Adder #(.width(3)) adder_1 (.a(MB_q), .b(MA_q), .out(adder_1_out));  // open: cin, cout
  Comparator #(.width(1)) comparator_1 (.a(ZA_q), .b(ZB_q), .eq(W0));  // open: gt, lt
  Comparator #(.width(3)) comparator_2 (.a(MA_q), .b(MB_q), .gt(W1));  // open: eq, lt
  Multiplexer #(.width(3), .enable("false")) multiplexer_2 (
    .in0(adder_1_out), .in1(subtractor_1_out), .out(multiplexer_2_out), .sel(S2));
  Multiplexer #(.width(3), .enable("false")) multiplexer_3 (.in0(MA_q), .in1(MB_q), .out(multiplexer_3_out), .sel(S1));
  Register #(.width(3)) MW (.D(multiplexer_2_out), .en(S3), .Q(out_9[2:0]), .clk(clock_1_out));  // open: clr
  Register #(.width(1)) ZB (.D(B[3]), .en(S0), .Q(ZB_q), .clk(clock_1_out));  // open: clr
  Multiplexer #(.width(3), .enable("false")) multiplexer_4 (.in0(MB_q), .in1(MA_q), .out(multiplexer_4_out), .sel(S1));
  Subtractor #(.width(3)) subtractor_1 (
    .a(multiplexer_4_out), .b(multiplexer_3_out), .out(subtractor_1_out));  // open: bin, bout
  Register #(.width(3)) MB (.D(B[2:0]), .en(S0), .Q(MB_q), .clk(clock_1_out));  // open: clr
  not not_1 (not_1_out, S1);
endmodule

module \Układ_sterujący  (
  input  SYNC,
  input  W0,
  input  W1,
  input  Set,
  output S0,
  output S1,
  output S2,
  output S3,
  output ACK
);

  wire and_1_out, and_2_out, and_3_out, and_4_out, and_5_out, and_6_out, and_7_out, and_8_out, clock_1_out,
       d_ff_1_q, d_ff_2_q, d_ff_3_q, d_ff_4_q, not_1_out, not_2_out, not_3_out, not_4_out, not_5_out,
       or_4_out, or_6_out;

  not not_1 (not_1_out, clock_1_out);
  Clock clock_1 (.out(clock_1_out));
  or or_1 (S0, and_7_out, and_1_out);
  D_Flip_Flop d_ff_1 (.clk(not_1_out), .D(S0), .Q(d_ff_1_q), .preset(Set));  // open: Qn, en, reset
  not not_2 (not_2_out, SYNC);
  and and_1 (and_1_out, not_2_out, d_ff_1_q);
  and and_2 (and_2_out, SYNC, d_ff_1_q);
  not not_3 (not_3_out, W0);
  and and_3 (and_3_out, not_3_out, and_2_out);
  and and_4 (and_4_out, W0, and_2_out);
  not not_4 (not_4_out, W1);
  and and_5 (and_5_out, not_4_out, and_3_out);
  and and_6 (and_6_out, W1, and_3_out);
  D_Flip_Flop d_ff_2 (.clk(not_1_out), .D(and_4_out), .Q(d_ff_2_q));  // open: Qn, preset, en, reset
  D_Flip_Flop d_ff_3 (.clk(not_1_out), .D(and_5_out), .Q(d_ff_3_q));  // open: Qn, preset, en, reset
  D_Flip_Flop d_ff_4 (.clk(not_1_out), .D(and_6_out), .Q(d_ff_4_q));  // open: Qn, preset, en, reset
  or or_2 (S3, d_ff_2_q, d_ff_4_q, d_ff_3_q);
  or or_3 (S2, d_ff_4_q, d_ff_3_q);
  or or_4 (or_4_out, d_ff_3_q, d_ff_4_q, d_ff_2_q);
  or or_5 (S1, d_ff_4_q, d_ff_2_q);
  or or_6 (or_6_out, or_4_out, and_8_out);
  D_Flip_Flop d_ff_5 (.clk(not_1_out), .D(or_6_out), .Q(ACK));  // open: Qn, preset, en, reset
  not not_5 (not_5_out, SYNC);
  and and_7 (and_7_out, not_5_out, ACK);
  and and_8 (and_8_out, SYNC, ACK);
endmodule
