// Logisim project Krawczyk Bartłomiej - Lab 6.circ as structural Verilog: 1 circuit, main circuit main
module main (
  input  SYNC,
  input  [3:0] xi,
  output WYN,
  output ACK,
  output [3:0] y1,
  output [3:0] y0
);

  wire CK_out, comparator_1_gt, counter_1_carry, multiplexer_3_out, nand_1_out, not_1_out, not_2_out,
       not_3_out, not_4_out, or_1_out;
  wire [0:0] comparator_2_lt;
  wire [1:0] rom_1_data_3;
  wire [2:0] counter_2_q, rom_1_data;
  wire [3:0] multiplexer_1_out, multiplexer_2_out;
  wire [10:3] rom_1_data_2;

  Multiplexer #(.width(4), .enable("false")) multiplexer_1 (
    .in0(y1), .in1(xi), .out(multiplexer_1_out), .sel(comparator_1_gt));
  Comparator #(.width(4), .mode("unsigned")) comparator_1 (.a(xi), .b(y1), .gt(comparator_1_gt));  // open: eq, lt
  Register #(.width(4)) RMAX (.D(multiplexer_1_out), .en(rom_1_data_2[6]), .Q(y1), .clk(CK_out), .clr(rom_1_data_2[5]));
  or or_1 (or_1_out, rom_1_data_2[4], rom_1_data_2[3]);
  Counter #(.width(4), .max('hf)) counter_1 (
    .load(or_1_out), .D(xi), .count(rom_1_data_2[3]), .carry(counter_1_carry), .clk(CK_out));  // open: Q, clr
  Multiplexer #(.select(2), .width(4), .enable("false")) multiplexer_2 (
    .in0(y0), .in1(xi), .in2(4'b1111), .in3(4'b1111), .out(multiplexer_2_out),
    .sel({rom_1_data_2[7], comparator_2_lt[0]}));
  Comparator #(.width(4), .mode("unsigned")) comparator_2 (.a(xi), .b(y0), .lt(comparator_2_lt[0]));  // open: gt, eq
  Register #(.width(4)) RMIN (.D(multiplexer_2_out), .en(rom_1_data_2[8]), .Q(y0), .clk(CK_out));  // open: clr
  Clock CK (.out(CK_out));
  not not_1 (not_1_out, SYNC);
  not not_2 (not_2_out, counter_1_carry);
  Multiplexer #(.select(2), .enable("false")) multiplexer_3 (
    .in0(SYNC), .in1(not_1_out), .in2(not_2_out), .in3(1'b0), .out(multiplexer_3_out), .sel(rom_1_data_3));
  not not_3 (not_3_out, multiplexer_3_out);
  not not_4 (not_4_out, CK_out);
  nand nand_1 (nand_1_out, rom_1_data_2[10], ACK);
  nand nand_2 (ACK, nand_1_out, rom_1_data_2[9]);
  Counter #(.width(3), .max('h7)) counter_2 (
    .load(not_3_out), .D(rom_1_data), .count(multiplexer_3_out), .Q(counter_2_q), .clk(not_4_out));  // open: carry, clr
  ROM #(.addrWidth(3), .dataWidth(14)) rom_1 (
    .addr(counter_2_q), .data({rom_1_data_3, WYN, rom_1_data_2, rom_1_data}));  // open: sel

  // Notes on the sheet:
  //   S1
  //   S0
  //   S3
  //   S2
  //   Bartłomiej Krawczyk
  //   S5
  //   S4
  //   S8
  //   S7
  //   S6
  //   contents of rom_1 (hex, n*v repeats v):
  //   3b0 1401 202 274e 1404 3602 1c06 3600
endmodule
